# Fritzing sketch Fritzing Sketch (saved by Fritzing 0.9.2b)

parts:
  M2 = Stepper Motor - Bipolar
  J1 = Basic Servo
  Raspberry_Pi1 = Raspberry Pi 2
  S1 = Toggle Switch [package=THT]
  S2 = Toggle Switch [package=THT]
  PWM1 = PCA9685 16x12-bit PWM Breakout
  M1 = Stepper Motor - Bipolar
  R1 = Resistor [tolerance=±5% resistance=10k package=THT]
  Pi2 = StepperHat
  R2 = Resistor [tolerance=±1% resistance=10k package=THT]  # not connected

nets:
  N1: M2.A, Pi2.connector4
  N2: M2.C, Pi2.connector2
  N3: M2.B, Pi2.connector3
  N4: M2.D, Pi2.connector1
  GND: J1.gnd, Raspberry_Pi1.GPIO3, Raspberry_Pi1.GND, Raspberry_Pi1.GPIO18, S1.L2, PWM1.no_name_yet#601, PWM1.no_name_yet#603, PWM1.no_name_yet#1000
  N5: J1.vcc, PWM1.no_name_yet#100
  N6: J1.pulse, PWM1.no_name_yet#0
  3V3: Raspberry_Pi1.3v3, Raspberry_Pi1.GPIO2, Raspberry_Pi1.3V3, Raspberry_Pi1.5V, PWM1.no_name_yet#604, PWM1.no_name_yet#605
  N7: Raspberry_Pi1.GPIO5, S2.COM
  N8: Raspberry_Pi1.GPIO6, S1.COM, R1.Pin_1
  N9: M1.A, Pi2.connector9
  N10: M1.C, Pi2.connector7
  N11: M1.B, Pi2.connector8
  N12: M1.D, Pi2.connector6

notes:
  Motor X
  Motor Y
  Pen Up-Down
  <--->
  GPIO
  External 5V
  Limit switch X (GPIO 5)
  Limit switch Y (GPIO 6)
  Adafruit Stepper HAT
  Adafruit I2C PWM
